# Fritzing sketch circuit (saved by Fritzing 0.7.10b)
breadboards: 1

parts:
  U2 = atmega328 [package=dip]
  S1 = Pushbutton [package="[SMD]"]
  R1 = 10k Ω Resistor [package=THT]
  R2 = Trimmer Potentiometer [maximum_resistance=10kΩ package=THT]
  R3 = 2.2k Ω Resistor [package=THT]
  R4 = 2.2k Ω Resistor [package=THT]
  LED2 = green LED - 5mm [package="5 mm [THT]"]
  LED3 = Red LED - 5mm
  R5 = Basic Photo-Resistor (Photocell) [package=THT]
  Q1 = npn-Powertransistor [package="TO220 [THT]"]
  J1 = Screw terminal - 2 pins [package=THT]
  R6 = 10k Ω Resistor [package=THT]
  J2 = Screw terminal - 2 pins [package=THT]
  M1 = DC Motor
  D1 = Rectifier Diode [part_number=1N4001 package="Melf DO-213 AB [SMD]"]
  J3 = Screw terminal - 2 pins [package=THT]
  R7 = Resistor [tolerance=±5% resistance=220 package="0603 [SMD]"]
  R8 = 10 Ω Resistor [package=THT]
  J4 = Screw terminal - 2 pins [package=THT]  # not connected
  J5 = Screw terminal - 2 pins [package=THT]

nets:
  N1: U2.RESET, S1.Pin_1, S1.Pin_2, R1.Pin_0
  N2: U2.D0_(RX), J3.pin2
  N3: U2.D1_(TX), J3.pin1
  N4: U2.VCC, R1.Pin_1
  N5: U2.GND#7, S1.Pin_3, S1.Pin_4
  N6: U2.D7, R4.Pin_0, LED2.cathode
  N7: U2.D8, R3.Pin_0
  N8: U2.D12, R6.Pin_0
  N9: U2.AVCC, U2.AREF, R2.leg2, R5.pin_1, J1.pin1, J5.pin1
  N10: U2.GND#21, R2.leg1, LED2.anode, LED3.anode, Q1.base, J1.pin2, J2.pin1, D1.anode
  N11: U2.A1, R8.Pin_1
  N12: U2.A2, R7.Pin_1
  N13: U2.A5, R2.wiper
  N14: R3.Pin_1, LED3.cathode
  N15: R5.pin_0, R7.Pin_0
  N16: Q1.collector, M1.pin_1, D1.cathode
  N17: Q1.emitter, R6.Pin_1
  N18: J2.pin2, M1.pin_2
  N19: R8.Pin_0, J5.pin2
